// Digital circuit 1B alu.dig as structural Verilog
module _1B_alu (
  input  A,
  input  B,
  input  Cin,
  input  Sub,
  output Sum,
  output Cout
);

  wire fulladder_1_p1, not_1_out;

  not not_1 (not_1_out, B);
  MUX mux_1 (.A(B), .B(not_1_out), .Sel(Sub));  // open: Out
  // FullAdder fulladder_1: pin names not known; wires that end beside it: fulladder_1_p1, A, fulladder_1_p1, Cin, Sum, Cout

  // Notes on the sheet:
  //   A: First Bit.
  //   B: Second bit to add or subtract from the first.
  //   Cin: What bit we will carry in.
  //   Sub: Determine if we are adding or subtracting.
endmodule
