// Digital circuit 8b ALU.dig as structural Verilog
module _8b_ALU (
  input  A_3,
  input  A_2,
  input  A_1,
  input  A_0,
  input  A_7,
  input  A_6,
  input  A_5,
  input  A_4,
  input  B_3,
  input  B_2,
  input  B_1,
  input  B_0,
  input  B_7,
  input  B_6,
  input  B_5,
  input  B_4,
  input  Sub,
  input  Cin,
  output Cout,
  output Out_6,
  output Out_5,
  output Out_4,
  output Out_3,
  output Out_2,
  output Out_0,
  output Out_1,
  output Out_7
);

  wire undriven, undriven_2, undriven_3, undriven_4, undriven_5, undriven_6, undriven_7;

  _1b_ALU _1b_alu_1 (.A(A_0), .B(B_0), .Cin(Cin), .Sub(Sub));  // open: Sum, Cout
  _1b_ALU _1b_alu_2 (.A(A_1), .B(B_1), .Cin(undriven_7), .Sub(Sub));  // open: Sum, Cout
  _1b_ALU _1b_alu_3 (.A(A_2), .B(B_2), .Cin(undriven), .Sub(Sub));  // open: Sum, Cout
  _1b_ALU _1b_alu_4 (.A(A_3), .B(B_3), .Cin(undriven_2), .Sub(Sub));  // open: Sum, Cout
  _1b_ALU _1b_alu_5 (.A(A_4), .B(B_4), .Cin(undriven_3), .Sub(Sub));  // open: Sum, Cout
  _1b_ALU _1b_alu_6 (.A(A_5), .B(B_5), .Cin(undriven_4), .Sub(Sub));  // open: Sum, Cout
  _1b_ALU _1b_alu_7 (.A(A_6), .B(B_6), .Cin(undriven_5), .Sub(Sub));  // open: Sum, Cout
  _1b_ALU _1b_alu_8 (.A(A_7), .B(B_7), .Cin(undriven_6), .Sub(Sub));  // open: Sum, Cout
endmodule
