// Digital circuit ALU_Project.dig as structural Verilog
module ALU_Project (
);

  HalfAdder halfadder_1 ();  // open: A, B, Sum, Carry
  FullAdder fulladder_1 ();  // open: A, B, CIn, Sum, COut
endmodule
