// Digital circuit FullAdder.dig as structural Verilog
module FullAdder (
  input  A,
  input  B,
  input  CIn,
  output Sum,
  output COut
);

  wire halfadder_1_p3, halfadder_1_p4, halfadder_2_p4;

  // HalfAdder halfadder_1: pin names not known; wires that end beside it: A, B, halfadder_1_p3, halfadder_1_p4
  // HalfAdder halfadder_2: pin names not known; wires that end beside it: halfadder_1_p3, CIn, Sum, halfadder_2_p4
  or or_1 (COut, halfadder_2_p4, halfadder_1_p4);
endmodule
