// Digital circuit alu_1bit.dig as structural Verilog
module alu_1bit (
  input  A,
  input  B,
  input  Cin,
  input  Sub,
  output Sum,
  output Cout
);

  wire full_adder_1_p1, not_1_out;

  not not_1 (not_1_out, B);
  mux mux_1 (.A(B), .B(not_1_out), .Sel(Sub));  // open: Out
  // full_adder full_adder_1: pin names not known; wires that end beside it: full_adder_1_p1, A, full_adder_1_p1, Cin, Sum, Cout

  // Notes on the sheet:
  //   A: First Bit.
  //   B: Second bit to add or subtract from the first.
  //   Cin: What bit we will carry in.
  //   Sub: Determine if we are adding or subtracting.
endmodule
