// Digital circuit full_adder.dig as structural Verilog
module full_adder (
  input  A,
  input  B,
  input  CIn,
  output Sum,
  output COut
);

  wire half_adder_1_p3, half_adder_1_p4, half_adder_2_p4;

  // half_adder half_adder_1: pin names not known; wires that end beside it: A, B, half_adder_1_p3, half_adder_1_p4
  // half_adder half_adder_2: pin names not known; wires that end beside it: half_adder_1_p3, CIn, Sum, half_adder_2_p4
  or or_1 (COut, half_adder_2_p4, half_adder_1_p4);
endmodule
