// Digital circuit mux.dig as structural Verilog
module mux (
  input  A,
  input  B,
  input  Sel,
  output Out
);

  wire and_1_out, and_2_out, not_1_out;

  not not_1 (not_1_out, Sel);
  and and_1 (and_1_out, A, not_1_out);
  and and_2 (and_2_out, Sel, B);
  or or_1 (Out, and_1_out, and_2_out);

  // Notes on the sheet:
  //   A: Option A
  //   B: Option B
  //   Sel: Pick between A and B
endmodule
