// Digital circuit alu_1bit.dig as structural Verilog
module alu_1bit (
  input  A,
  input  B,
  input  Cin,
  input  Sub,
  output Cout,
  output Sum
);

  wire and_1_out, and_2_out, xor_1_out, xor_2_out;

  xor xor_1 (xor_1_out, B, Sub);
  xor xor_2 (xor_2_out, xor_1_out, A);
  and and_1 (and_1_out, xor_1_out, A);
  and and_2 (and_2_out, xor_2_out, Cin);
  xor xor_3 (Sum, xor_2_out, Cin);
  or or_1 (Cout, and_2_out, and_1_out);
endmodule
