// Digital circuit alu_8bit.dig as structural Verilog
module alu_8bit (
  input  A_3,
  input  A_2,
  input  A_1,
  input  A_0,
  input  A_7,
  input  A_6,
  input  A_5,
  input  A_4,
  input  B_3,
  input  B_2,
  input  B_1,
  input  B_0,
  input  B_7,
  input  B_6,
  input  B_5,
  input  B_4,
  input  Sub,
  input  Cin,
  output Sum_0,
  output Sum_1,
  output Sum_2,
  output Sum_3,
  output Sum_4,
  output Sum_5,
  output Sum_6,
  output Sum_7,
  output Cout_1
);

  wire and_1_out, and_2_out, and_3_out, and_4_out, and_5_out, and_6_out, and_7_out, and_8_out, and_9_out,
       and_10_out, and_11_out, and_12_out, and_13_out, and_14_out, and_15_out, and_16_out, or_1_out,
       or_2_out, or_3_out, or_4_out, or_5_out, or_6_out, or_7_out, xor_1_out, xor_2_out, xor_3_out,
       xor_4_out, xor_5_out, xor_6_out, xor_7_out, xor_8_out, xor_9_out, xor_10_out, xor_11_out, xor_12_out,
       xor_13_out, xor_14_out, xor_15_out, xor_16_out;

  xor xor_1 (xor_1_out, B_0, Sub);
  xor xor_2 (xor_2_out, B_1, Sub);
  xor xor_3 (xor_3_out, B_2, Sub);
  xor xor_4 (xor_4_out, B_3, Sub);
  xor xor_5 (xor_5_out, B_4, Sub);
  xor xor_6 (xor_6_out, B_5, Sub);
  xor xor_7 (xor_7_out, B_6, Sub);
  xor xor_8 (xor_8_out, B_7, Sub);
  xor xor_9 (xor_9_out, xor_1_out, A_0);
  and and_1 (and_1_out, xor_1_out, A_0);
  xor xor_10 (xor_10_out, xor_2_out, A_1);
  and and_2 (and_2_out, xor_2_out, A_1);
  xor xor_11 (xor_11_out, xor_3_out, A_2);
  and and_3 (and_3_out, xor_3_out, A_2);
  xor xor_12 (xor_12_out, xor_4_out, A_3);
  and and_4 (and_4_out, xor_4_out, A_3);
  xor xor_13 (xor_13_out, xor_5_out, A_4);
  and and_5 (and_5_out, xor_5_out, A_4);
  xor xor_14 (xor_14_out, xor_6_out, A_5);
  and and_6 (and_6_out, xor_6_out, A_5);
  xor xor_15 (xor_15_out, xor_7_out, A_6);
  and and_7 (and_7_out, xor_7_out, A_6);
  xor xor_16 (xor_16_out, xor_8_out, A_7);
  and and_8 (and_8_out, xor_8_out, A_7);
  and and_9 (and_9_out, xor_9_out, Cin);
  and and_10 (and_10_out, xor_10_out, or_1_out);
  and and_11 (and_11_out, xor_11_out, or_2_out);
  and and_12 (and_12_out, xor_12_out, or_3_out);
  and and_13 (and_13_out, xor_13_out, or_4_out);
  and and_14 (and_14_out, xor_14_out, or_5_out);
  and and_15 (and_15_out, xor_15_out, or_6_out);
  and and_16 (and_16_out, xor_16_out, or_7_out);
  xor xor_17 (Sum_0, xor_9_out, Cin);
  or or_1 (or_1_out, and_9_out, and_1_out);
  xor xor_18 (Sum_1, xor_10_out, or_1_out);
  or or_2 (or_2_out, and_10_out, and_2_out);
  xor xor_19 (Sum_2, xor_11_out, or_2_out);
  or or_3 (or_3_out, and_11_out, and_3_out);
  xor xor_20 (Sum_3, xor_12_out, or_3_out);
  or or_4 (or_4_out, and_12_out, and_4_out);
  xor xor_21 (Sum_4, xor_13_out, or_4_out);
  or or_5 (or_5_out, and_13_out, and_5_out);
  xor xor_22 (Sum_5, xor_14_out, or_5_out);
  or or_6 (or_6_out, and_14_out, and_6_out);
  xor xor_23 (Sum_6, xor_15_out, or_6_out);
  or or_7 (or_7_out, and_15_out, and_7_out);
  xor xor_24 (Sum_7, xor_16_out, or_7_out);
  or or_8 (Cout_1, and_16_out, and_8_out);
endmodule
