// Digital circuit 2to4_mux.dig as structural Verilog
module _2to4_mux (
  input  OP_1,
  input  OP_0,
  input  In1,
  input  In2,
  input  In3,
  input  In4,
  output Result
);

  wire and_1_out, and_2_out, and_3_out, and_4_out, not_1_out, not_2_out, not_3_out, not_4_out;

  not not_1 (not_1_out, OP_0);
  not not_2 (not_2_out, OP_1);
  not not_3 (not_3_out, OP_1);
  not not_4 (not_4_out, OP_0);
  and and_1 (and_1_out, not_1_out, In1, not_2_out);
  and and_2 (and_2_out, OP_0, In2, not_3_out);
  and and_3 (and_3_out, not_4_out, In3, OP_1);
  and and_4 (and_4_out, OP_0, In4, OP_1);
  or or_1 (Result, and_1_out, and_2_out, and_3_out, and_4_out);
endmodule
