// Digital circuit alu_1bit.dig as structural Verilog
module alu_1bit (
  input  A,
  input  B,
  input  InvertA,
  input  InvertB,
  input  OP_1,
  input  OP_0,
  input  Cin,
  output Result,
  output Cout
);

  wire and_1_out, and_2_out, or_1_out, xor_1_out, xor_2_out, xor_3_out, xor_4_out;

  xor xor_1 (xor_1_out, A, InvertA);
  xor xor_2 (xor_2_out, InvertB, B);
  and and_1 (and_1_out, xor_1_out, xor_2_out);
  or or_1 (or_1_out, xor_1_out, xor_2_out);
  xor xor_3 (xor_3_out, xor_1_out, xor_2_out);
  and and_2 (and_2_out, Cin, xor_3_out);
  xor xor_4 (xor_4_out, Cin, xor_3_out);
  or or_2 (Cout, and_1_out, and_2_out);
  // _2to4_mux _2to4_mux_1: pin names not known; wires that end beside it: and_1_out, or_1_out, xor_3_out, xor_4_out, OP_1, OP_0, Result
endmodule
