// Digital circuit alu_8bit.dig as structural Verilog
module alu_8bit (
  input  OP_1,
  input  OP_0,
  input  Cin,
  input  B_0,
  input  A_0,
  input  A_1,
  input  B_1,
  input  B_2,
  input  A_2,
  input  B_3,
  input  A_3,
  input  B_4,
  input  A_4,
  input  B_5,
  input  A_5,
  input  B_6,
  input  B_7,
  input  A_6,
  input  A_7,
  input  AInvert,
  input  BInvert,
  output Sum_0,
  output Sum_1,
  output Sum_2,
  output Sum_3,
  output Sum_4,
  output Sum_5,
  output Sum_6,
  output Sum_7,
  output Cout_1
);

  wire alu_1bit_1_p6, alu_1bit_2_p6, alu_1bit_3_p6, alu_1bit_4_p6, alu_1bit_5_p6, alu_1bit_6_p6,
       alu_1bit_7_p6;

  // alu_1bit alu_1bit_1: pin names not known; wires that end beside it: A_0, B_0, AInvert, BInvert, Cin, alu_1bit_1_p6, OP_1, OP_0, Sum_0
  // alu_1bit alu_1bit_2: pin names not known; wires that end beside it: A_1, B_1, AInvert, BInvert, alu_1bit_1_p6, alu_1bit_2_p6, OP_1, OP_0, Sum_1
  // alu_1bit alu_1bit_3: pin names not known; wires that end beside it: A_2, B_2, AInvert, BInvert, alu_1bit_2_p6, alu_1bit_3_p6, OP_1, OP_0, Sum_2
  // alu_1bit alu_1bit_4: pin names not known; wires that end beside it: A_3, B_3, AInvert, BInvert, alu_1bit_3_p6, alu_1bit_4_p6, OP_1, OP_0, Sum_3
  // alu_1bit alu_1bit_5: pin names not known; wires that end beside it: A_4, B_4, AInvert, BInvert, alu_1bit_4_p6, alu_1bit_5_p6, OP_1, OP_0, Sum_4
  // alu_1bit alu_1bit_6: pin names not known; wires that end beside it: A_5, B_5, AInvert, BInvert, alu_1bit_5_p6, alu_1bit_6_p6, OP_1, OP_0, Sum_5
  // alu_1bit alu_1bit_7: pin names not known; wires that end beside it: A_6, B_6, AInvert, BInvert, alu_1bit_6_p6, alu_1bit_7_p6, OP_1, OP_0, Sum_6
  // alu_1bit alu_1bit_8: pin names not known; wires that end beside it: A_7, B_7, AInvert, BInvert, alu_1bit_7_p6, Cout_1, OP_1, OP_0, Sum_7
endmodule
