// Digital circuit 3to8_mux.dig as structural Verilog
module _3to8_mux (
  input  OP_0,
  input  OP_2,
  input  OP_1,
  input  In5,
  input  In6,
  input  In7,
  input  In8,
  input  In1,
  input  In2,
  input  In3,
  input  In4,
  output Result
);

  wire and_1_out, and_2_out, and_3_out, and_4_out, and_5_out, and_6_out, and_7_out, and_8_out, not_1_out,
       not_2_out, not_3_out, not_4_out, not_5_out, not_6_out, not_7_out, not_8_out, not_9_out, not_10_out,
       not_11_out, not_12_out;

  not not_1 (not_1_out, OP_0);
  not not_2 (not_2_out, OP_1);
  not not_3 (not_3_out, OP_2);
  not not_4 (not_4_out, OP_1);
  not not_5 (not_5_out, OP_2);
  not not_6 (not_6_out, OP_0);
  not not_7 (not_7_out, OP_2);
  not not_8 (not_8_out, OP_2);
  not not_9 (not_9_out, OP_0);
  not not_10 (not_10_out, OP_1);
  not not_11 (not_11_out, OP_1);
  not not_12 (not_12_out, OP_0);
  and and_1 (and_1_out, not_1_out, not_2_out, not_3_out, In1);
  and and_2 (and_2_out, OP_0, not_4_out, not_5_out, In2);
  and and_3 (and_3_out, not_6_out, OP_1, not_7_out, In3);
  and and_4 (and_4_out, OP_0, OP_1, not_8_out, In4);
  and and_5 (and_5_out, not_9_out, not_10_out, OP_2, In5);
  and and_6 (and_6_out, OP_0, not_11_out, OP_2, In6);
  and and_7 (and_7_out, not_12_out, OP_1, OP_2, In7);
  and and_8 (and_8_out, OP_0, OP_1, OP_2, In8);
  or or_1 (Result, and_1_out, and_2_out, and_3_out, and_4_out, and_5_out, and_6_out, and_7_out, and_8_out);
endmodule
