// Digital circuit alu_8bit.dig as structural Verilog
module alu_8bit (
  input  Cin,
  input  B_0,
  input  A_0,
  input  AInvert,
  input  BInvert,
  input  OP_1,
  input  OP_0,
  input  OP_2,
  input  B_1,
  input  A_1,
  input  B_2,
  input  A_2,
  input  B_3,
  input  A_3,
  input  B_4,
  input  A_4,
  input  B_5,
  input  A_5,
  input  B_6,
  input  A_6,
  input  B_7,
  input  A_7,
  output Result_0,
  output Result_1,
  output Result_2,
  output Result_3,
  output Result_4,
  output Result_5,
  output Result_6,
  output Result_7,
  output Cout
);

  wire alu_1bit_1_p6, alu_1bit_2_p6, alu_1bit_3_p6, alu_1bit_4_p6, alu_1bit_5_p6, alu_1bit_6_p6,
       alu_1bit_7_p6;

  // alu_1bit alu_1bit_1: pin names not known; wires that end beside it: A_0, B_0, AInvert, BInvert, Cin, alu_1bit_1_p6, OP_2, OP_1, OP_0, Result_0
  // alu_1bit alu_1bit_2: pin names not known; wires that end beside it: A_1, B_1, AInvert, BInvert, alu_1bit_1_p6, alu_1bit_2_p6, OP_2, OP_1, OP_0, Result_1
  // alu_1bit alu_1bit_3: pin names not known; wires that end beside it: A_2, B_2, AInvert, BInvert, alu_1bit_2_p6, alu_1bit_3_p6, OP_2, OP_1, OP_0, Result_2
  // alu_1bit alu_1bit_4: pin names not known; wires that end beside it: A_3, B_3, AInvert, BInvert, alu_1bit_3_p6, alu_1bit_4_p6, OP_2, OP_1, OP_0, Result_3
  // alu_1bit alu_1bit_5: pin names not known; wires that end beside it: A_4, B_4, AInvert, BInvert, alu_1bit_4_p6, alu_1bit_5_p6, OP_2, OP_1, OP_0, Result_4
  // alu_1bit alu_1bit_6: pin names not known; wires that end beside it: A_5, B_5, AInvert, BInvert, alu_1bit_5_p6, alu_1bit_6_p6, OP_2, OP_1, OP_0, Result_5
  // alu_1bit alu_1bit_7: pin names not known; wires that end beside it: A_6, B_6, AInvert, BInvert, alu_1bit_6_p6, alu_1bit_7_p6, OP_2, OP_1, OP_0, Result_6
  // alu_1bit alu_1bit_8: pin names not known; wires that end beside it: A_7, B_7, AInvert, BInvert, alu_1bit_7_p6, Cout, OP_2, OP_1, OP_0, Result_7
endmodule
