// Digital circuit alu_8bit_full.dig as structural Verilog
module alu_8bit_full (
  input  [7:0] B,
  input  [7:0] A,
  input  [3:0] OP,
  output Cout,
  output [7:0] Result
);

  wire alu_8bit_1_p10, InvA_out, InvB_out;
  wire [2:0] alu_8bit_1_p13;

  LookUpTable InvA (.in0(OP[0]), .in1(OP[1]), .in2(OP[2]), .in3(OP[3]), .out(InvA_out));
  LookUpTable InvB (.in0(OP[0]), .in1(OP[1]), .in2(OP[2]), .in3(OP[3]), .out(InvB_out));
  // alu_8bit alu_8bit_1: pin names not known; wires that end beside it: A[0], B[0], A[1], B[1], A[2], B[2], A[3], InvA_out, InvB_out, alu_8bit_1_p10, alu_8bit_1_p13[2], alu_8bit_1_p13[1], alu_8bit_1_p13[0], Result[0], Result[1]
  LookUpTable Cin (.in0(OP[0]), .in1(OP[1]), .in2(OP[2]), .in3(OP[3]), .out(alu_8bit_1_p10));
  LookUpTable #(.Bits(3)) u_OP (.in0(OP[0]), .in1(OP[1]), .in2(OP[2]), .in3(OP[3]), .out(alu_8bit_1_p13));

  // Notes on the sheet:
  //   contents of InvA (hex, n*v repeats v):
  //   0,8,0,0,0,1,1
  //   contents of InvB (hex, n*v repeats v):
  //   0,8,0,0,1,0,a,1
  //   contents of Cin (hex, n*v repeats v):
  //   0,8,0,0,1,b,a,1
  //   contents of OP (hex, n*v repeats v):
  //   0,1,2,3,3,3,4,5,4,5,6,7
endmodule
